# Fritzing sketch schemat (saved by Fritzing 0.9.9b)
breadboards: 1

parts:
  Mod1 = Raspberry Pi 4B
  Part1 = Adafruit VL530X Time of Flight Distance Sensor [part_number="Adafruit #3317"]
  J1 = Basic Servo
  Part2 = Logic Level Converter
  R1 = Resistor [tolerance=±5% resistance=10k package="0402 [SMD]"]
  R3 = Resistor [tolerance=±5% resistance=4.8k package="0402 [SMD]"]
  R4 = Resistor [tolerance=±5% resistance=4.8k package="0402 [SMD]"]

nets:
  3V3: Mod1.3V3, Part1.VCC, Part2.LV, R1.Pin_0, R3.Pin_0, R4.Pin_0
  5V: Mod1.5V, J1.vcc, Part2.HV
  N1: Mod1.GPIO2, Part1.SDA, R3.Pin_1
  N2: Mod1.GPIO3, Part1.SCL, R4.Pin_1
  GND: Mod1.GND, Part1.GND, Part2.GND
  N3: Mod1.GPIO19, Part2.TX2_LV
  N4: Part1.XSHUT, R1.Pin_1
  N5: J1.pulse, Part2.TX2_HV

custom parts:
  Adafruit VL530X Time of Flight Distance Sensor: The VL53L0X is a Time of Flight distance sensor like no other you've used! The sensor contains a very tiny invisible laser source, and a matching sensor. The VL53L0X can detect the "time of flight", or how long the light has taken to bounce back to the sensor. Since it uses a very narrow light source, it is good for determining distance of only the surface directly in front of it. Unlike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
